# Fritzing sketch CoheteDeAguaFritzing (saved by Fritzing 0.9.6b)
breadboards: 1

parts:
  Componente1 = Arduino Uno (Rev3)
  Componente2 = Barometric Pressure Sensor - BMP180 Breakout (GY-68)
  M1 = Dagu DGServo 9g (Pan and tilt) [part_number=RS001B]
  Mod1 = Passive Buzzer
  microSD1 = MicroSD Card Module  # not connected

nets:
  N1: Componente1.D8, M1.pulse
  N2: Componente1.D9_PWM, Mod1.S
  3V3: Componente1.3V3, Componente2.VCC
  5V: Componente1.5V, M1.vcc, Mod1.NC
  GND: Componente1.GND, Componente2.GND, M1.gnd, Mod1.-
